// Logisim project circuit_.circ as structural Verilog: 2 circuits, main circuit main
module main (
);

  wire AC_B, ALU_out, and_1_out, and_2_out, and_3_out, and_4_out, and_5_out, and_6_out, and_7_out, and_8_out,
       and_9_out, and_10_out, and_11_out, and_12_out, and_13_out, and_14_out, and_16_out, and_17_out,
       and_18_out, and_19_out, and_20_out, and_21_out, and_22_out, and_23_out, and_24_out, and_25_out,
       and_26_out, and_27_out, and_28_out, and_29_out, and_30_out, and_31_out, and_32_out, and_33_out,
       and_34_out, and_35_out, and_36_out, and_37_out, and_38_out, and_39_out, and_40_out, and_41_out,
       and_42_out, and_43_out, and_44_out, and_45_out, and_46_out, AR_B, clk, clks, COMMON_BUS_out,
       comparator_1_eq, comparator_2_eq, comparator_3_eq, CONTROL_UNIT_out, D0, D1, D2, D3, D4, D5, D6, D7,
       D8, D9, D10, D11, D12, D13, D14, D15, DATA_UNIT_out, decoder_1_out0, decoder_1_out1, decoder_1_out2,
       decoder_1_out3, decoder_1_out4, decoder_1_out5, decoder_1_out6, decoder_1_out7, E, FGI, FGO,
       FLAGS_out, I, INPUT_OUTPUT_out, IR_B, MEM_B, MEMORY_out, not_2_out, or_1_out, or_2_out, or_3_out,
       or_4_out, or_5_out, or_6_out, or_7_out, or_8_out, or_9_out, or_10_out, or_11_out, or_12_out,
       or_13_out, or_14_out, or_15_out, or_16_out, or_17_out, or_18_out, or_20_out, or_24_out, or_25_out,
       or_26_out, or_27_out, or_29_out, PC_B, REGISTERS_out, S, T0, T1, T3, T4, T5, T6, T7, undriven,
       undriven_2, Z;
  wire [1:0] priority_encoder_1_out, priority_encoder_2_out;
  wire [2:0] priority_encoder_3_out, t_ff_1_q;
  wire [7:0] dipswitch_1_sw1, INPR, OUTR_q;
  wire [10:0] adder_2_out, adder_4_out, AR, controlled_buffer_1_out, multiplexer_1_out, multiplexer_4_out,
       multiplexer_7_out, PC;
  wire [15:0] AC, adder_1_out, adder_3_out, ALU_O, and_15_out, B, bit_extender_1_out, DR, IR, MEM,
       multiplexer_3_out, multiplexer_6_out, not_1_out;
  wire [17:0] multiplexer_2_out;
  wire [17:16] ram_1_dout;

  Clock clock_1 (.out(clks));
  buf DATA_UNIT (DATA_UNIT_out, DATA_UNIT_out);
  buf REGISTERS (REGISTERS_out, REGISTERS_out);
  Register #(.width(16)) u_IR (.D(MEM), .en(T1), .clk(clk), .Q({IR[15:12], I, IR[10:0]}));  // open: clr
  buf MEMORY (MEMORY_out, MEMORY_out);
  and and_1 (and_1_out, D9, T4);
  Demultiplexer #(.select(4)) demultiplexer_1 (
    .out0(D0), .out1(D1), .out2(D2), .out3(D3), .out4(D4), .out5(D5), .out6(D6), .out7(D7), .out8(D8),
    .out9(D9), .out10(D10), .out11(D11), .out12(D12), .out13(D13), .out14(D14), .out15(D15), .in(1'b1),
    .sel(IR[15:12]));  // open: en
  and and_2 (and_2_out, T4, D1);
  and and_3 (and_3_out, T4, D9);
  and and_4 (and_4_out, D7, T6);
  assign controlled_buffer_1_out = or_1_out ? multiplexer_1_out : 11'bz;  // Controlled_Buffer controlled_buffer_1
  Multiplexer #(.width(11)) multiplexer_1 (.in0(PC), .in1(AR), .out(multiplexer_1_out), .sel(or_4_out), .en(or_1_out));
  or or_1 (or_1_out, PC_B, or_4_out);
  or or_2 (or_2_out, and_2_out, and_4_out, and_3_out);
  RAM #(.addrWidth(11), .dataWidth(18), .trigger("falling"), .databus("bibus")) ram_1 (
    .addr(controlled_buffer_1_out), .we(or_2_out), .oe(MEM_B), .clk(clk), .din(multiplexer_2_out),
    .dout({ram_1_dout, MEM}));
  Multiplexer #(.select(2), .width(18)) multiplexer_2 (
    .in0({{7{1'b0}}, PC}), .in1({2'b00, AC}), .in2({2'b00, DR}), .out(multiplexer_2_out),
    .sel(priority_encoder_1_out), .en(or_3_out));  // open: in3
  Priority_Encoder #(.select(2)) priority_encoder_1 (
    .in0(and_1_out), .in1(and_5_out), .in2(and_4_out), .out(priority_encoder_1_out));  // open: in3
  and and_5 (and_5_out, D1, T4);
  or or_3 (or_3_out, and_4_out, and_1_out, PC_B, and_5_out);
  or or_4 (or_4_out, MEM_B, or_2_out);
  and and_6 (and_6_out, T4, D4);
  and and_7 (and_7_out, T4, D8);
  or or_5 (or_5_out, and_7_out, and_8_out);
  and and_8 (and_8_out, T5, D9);
  and and_9 (and_9_out, T4, D3);
  or or_6 (or_6_out, and_9_out, and_6_out, and_10_out);
  or or_7 (or_7_out, or_6_out, and_14_out);
  and and_10 (and_10_out, T4, D7);
  or or_8 (or_8_out, or_5_out, or_10_out);
  Register #(.width(16)) u_DR (.D(multiplexer_3_out), .en(or_7_out), .clk(clk), .Q(DR), .clr(1'b0));
  Register #(.width(11)) u_PC (.D(multiplexer_4_out), .en(or_8_out), .clk(clk), .Q(PC), .clr(undriven));
  Comparator #(.width(1)) comparator_1 (.a(FGO), .b(1'b1), .eq(comparator_1_eq));  // open: gt, lt
  Comparator #(.width(1)) comparator_2 (.a(FGI), .b(1'b1), .eq(comparator_2_eq));  // open: gt, lt
  Comparator #(.width(16)) comparator_3 (.a(DR), .b({16{1'b0}}), .eq(comparator_3_eq));  // open: gt, lt
  buf ALU (ALU_out, ALU_out);
  buf FLAGS (FLAGS_out, FLAGS_out);
  and and_11 (and_11_out, T3, comparator_1_eq, D14);
  and and_12 (and_12_out, T3, comparator_2_eq, D13);
  and and_13 (and_13_out, T6, comparator_3_eq, D7);
  assign bit_extender_1_out = {{8{1'b0}}, INPR};  // Bit_Extender bit_extender_1
  LED led_1 (.in(S));
  Multiplexer #(.width(16)) multiplexer_3 (
    .in0(B), .in1(adder_1_out), .out(multiplexer_3_out), .sel(and_14_out), .en(or_9_out));
  or or_9 (or_9_out, or_6_out, and_14_out);
  Adder #(.width(16)) adder_1 (.a(DR), .b(16'h1), .out(adder_1_out));  // open: cin, cout
  and and_14 (and_14_out, D7, T5);
  Adder #(.width(11)) adder_2 (.a(PC), .b(11'h1), .out(adder_2_out));  // open: cin, cout
  or or_10 (or_10_out, and_11_out, and_12_out, and_13_out, T1);
  assign and_15_out = AC & DR;  // AND_Gate and_15, 16 bits wide
  assign not_1_out = ~AC;  // NOT_Gate not_1, 16 bits wide
  and and_16 (and_16_out, T5, D3);
  and and_17 (and_17_out, T5, D4);
  and and_18 (and_18_out, T3, D11);
  and and_19 (and_19_out, T3, D5);
  LED led_2 (.in(Z));
  LED led_3 (.in(I));
  Multiplexer #(.width(11)) multiplexer_4 (
    .in0(B[10:0]), .in1(adder_2_out), .out(multiplexer_4_out), .sel(or_10_out), .en(or_11_out));
  or or_11 (or_11_out, or_5_out, or_10_out);
  Adder #(.width(16)) adder_3 (.a(AC), .b(DR), .out(adder_3_out), .cout(E));  // open: cin
  Priority_Encoder #(.select(2)) priority_encoder_2 (
    .in0(and_16_out), .in1(and_17_out), .in2(and_18_out), .in3(and_19_out), .out(priority_encoder_2_out));  // open: gs, en_out, en_in
  LED led_4 (.in(E));
  not not_2 (not_2_out, or_12_out);
  Multiplexer #(.select(2), .width(16)) multiplexer_5 (
    .in0(adder_3_out), .in1(and_15_out), .in2(bit_extender_1_out), .in3(not_1_out), .out(ALU_O),
    .sel(priority_encoder_2_out), .en(or_12_out));
  or or_12 (or_12_out, and_16_out, and_17_out, and_18_out, and_19_out);
  LED led_5 (.in(FGI));
  or or_13 (or_13_out, D0, D1, D3, D4, D7, D8, D9);
  LED led_6 (.in(FGO));
  and and_20 (and_20_out, T4, D0);
  and and_21 (and_21_out, T5, D3);
  nor nor_1 (Z, not_2_out, ALU_O[0], ALU_O[1], ALU_O[2], ALU_O[3], ALU_O[4], ALU_O[5], ALU_O[6], ALU_O[7], ALU_O[8], ALU_O[9], ALU_O[10], ALU_O[11], ALU_O[12], ALU_O[13], ALU_O[14], ALU_O[15]);
  and and_22 (and_22_out, T5, D4);
  or or_14 (or_14_out, and_20_out, and_22_out, and_21_out, and_23_out, and_24_out);
  and and_23 (and_23_out, T3, D5);
  and and_24 (and_24_out, T3, D11);
  or or_15 (or_15_out, T0, IR_B, and_25_out);
  or or_16 (or_16_out, or_15_out, and_31_out);
  and and_25 (and_25_out, T3, I, or_13_out);
  buf INPUT_OUTPUT (INPUT_OUTPUT_out, undriven_2);
  DipSwitch dipswitch_1 (
    .sw1(dipswitch_1_sw1[0]), .sw2(dipswitch_1_sw1[1]), .sw3(dipswitch_1_sw1[2]), .sw4(dipswitch_1_sw1[3]),
    .sw5(dipswitch_1_sw1[4]), .sw6(dipswitch_1_sw1[5]), .sw7(dipswitch_1_sw1[6]), .sw8(dipswitch_1_sw1[7]));
  assign clk = S ? clks : 1'bz;  // Controlled_Buffer controlled_buffer_2
  and and_26 (and_26_out, T3, D15);
  Register #(.width(16)) u_AC (.D(multiplexer_6_out), .en(or_14_out), .clk(clk), .Q(AC), .clr(and_27_out));
  and and_27 (and_27_out, D6, T3);
  Register #(.width(11)) u_AR (.D(multiplexer_7_out), .en(or_16_out), .clk(clk), .Q(AR));  // open: clr
  Register OUTR (.D(AC[7:0]), .en(and_28_out), .clk(clk), .Q(OUTR_q));  // open: clr
  and and_28 (and_28_out, D12, IR_B);
  and and_29 (and_29_out, D11, IR_B);
  not not_3 (S, and_26_out);
  LED led_7 (.in(OUTR_q[7]));
  Register u_INPR (.D(dipswitch_1_sw1), .en(and_29_out), .clk(clk), .Q(INPR));  // open: clr
  Multiplexer #(.width(16)) multiplexer_6 (
    .in0(ALU_O), .in1(MEM), .out(multiplexer_6_out), .sel(and_30_out), .en(or_17_out));
  or or_17 (or_17_out, or_14_out, and_30_out);
  and and_30 (and_30_out, D0, T4);
  Multiplexer #(.width(11)) multiplexer_7 (
    .in0(B[10:0]), .in1(adder_4_out), .out(multiplexer_7_out), .sel(and_31_out), .en(or_18_out));
  Adder #(.width(11)) adder_4 (.a(AR), .b(11'h1), .out(adder_4_out));  // open: cin, cout
  and and_31 (and_31_out, D9, T4);
  LED led_8 (.in(OUTR_q[4]));
  LED led_9 (.in(OUTR_q[3]));
  LED led_10 (.in(OUTR_q[6]));
  LED led_11 (.in(OUTR_q[5]));
  nor nor_2 (FGO, OUTR_q[7], OUTR_q[6], OUTR_q[5], OUTR_q[4], OUTR_q[3], OUTR_q[2], OUTR_q[1], OUTR_q[0]);
  or or_18 (or_18_out, or_15_out, and_31_out);
  LED led_12 (.in(OUTR_q[2]));
  LED led_13 (.in(OUTR_q[0]));
  LED led_14 (.in(OUTR_q[1]));
  or or_19 (FGI, dipswitch_1_sw1[7], dipswitch_1_sw1[6], dipswitch_1_sw1[5], dipswitch_1_sw1[4], dipswitch_1_sw1[3], dipswitch_1_sw1[2], dipswitch_1_sw1[1], dipswitch_1_sw1[0]);
  buf CONTROL_UNIT (CONTROL_UNIT_out, CONTROL_UNIT_out);
  D_Flip_Flop d_ff_1 (.D(decoder_1_out0), .clk(clk), .Q(T0), .reset(or_20_out));  // open: Qn, preset
  or or_20 (or_20_out, and_37_out, and_38_out, and_39_out, and_40_out);
  buf COMMON_BUS (COMMON_BUS_out, COMMON_BUS_out);
  and and_32 (and_32_out, T4, D8);
  and and_33 (and_33_out, T5, D9);
  and and_34 (and_34_out, T4, D1);
  and and_35 (and_35_out, T3, D12);
  and and_36 (and_36_out, T4, D9);
  D_Flip_Flop d_ff_2 (.D(decoder_1_out1), .clk(clk), .Q(T1), .reset(or_20_out));  // open: Qn, preset
  and and_37 (and_37_out, T4, or_27_out);
  and and_38 (and_38_out, T5, or_25_out);
  and and_39 (and_39_out, T6, or_26_out);
  and and_40 (and_40_out, T7, D7);
  or or_21 (AR_B, and_32_out, and_33_out);
  or or_22 (AC_B, and_34_out, and_35_out);
  or or_23 (PC_B, T0, and_36_out);
  or or_24 (or_24_out, D0, D1, D3, D4, D7, D8, D9);
  T_Flip_Flop t_ff_1 (.T(1'b1), .clk(clk), .Q(t_ff_1_q[0]), .reset(or_20_out));  // open: Qn, preset
  Decoder #(.select(3)) decoder_1 (
    .out0(decoder_1_out0), .out1(decoder_1_out1), .out2(decoder_1_out2), .out3(decoder_1_out3),
    .out4(decoder_1_out4), .out5(decoder_1_out5), .out6(decoder_1_out6), .out7(decoder_1_out7), .sel(t_ff_1_q));  // open: en
  D_Flip_Flop d_ff_3 (.D(decoder_1_out2), .clk(clk), .Q(IR_B), .reset(or_20_out));  // open: Qn, preset
  or or_25 (or_25_out, D0, D1, D8);
  or or_26 (or_26_out, D3, D4, D9);
  T_Flip_Flop t_ff_2 (.T(t_ff_1_q[0]), .clk(clk), .Q(t_ff_1_q[1]), .reset(or_20_out));  // open: Qn, preset
  D_Flip_Flop d_ff_4 (.D(decoder_1_out3), .clk(clk), .Q(T3), .reset(or_20_out));  // open: Qn, preset
  and and_41 (and_41_out, D0, T4);
  and and_42 (and_42_out, T4, D3);
  and and_43 (and_43_out, T4, D4);
  and and_44 (and_44_out, T4, D7);
  and and_45 (and_45_out, T3, I, or_24_out);
  T_Flip_Flop t_ff_3 (.T(and_46_out), .clk(clk), .Q(t_ff_1_q[2]), .reset(or_20_out));  // open: Qn, preset
  and and_46 (and_46_out, t_ff_1_q[1], t_ff_1_q[0]);
  D_Flip_Flop d_ff_5 (.D(decoder_1_out4), .clk(clk), .Q(T4), .reset(or_20_out));  // open: Qn, preset
  or or_27 (or_27_out, D11, D5, D6, D10, D13, D14, D15, D12);
  or or_28 (MEM_B, T1, and_41_out, and_42_out, and_43_out, and_44_out, and_45_out);
  D_Flip_Flop d_ff_6 (.D(decoder_1_out5), .clk(clk), .Q(T5), .reset(or_20_out));  // open: Qn, preset
  Priority_Encoder priority_encoder_3 (
    .in2(AC_B), .in3(IR_B), .in4(PC_B), .in5(AR_B), .in6(MEM_B), .out(priority_encoder_3_out));  // open: in0, in1, in7, en_in, gs, en_out
  D_Flip_Flop d_ff_7 (.D(decoder_1_out6), .clk(clk), .Q(T6), .reset(or_20_out));  // open: Qn, preset
  Multiplexer #(.select(3), .width(16)) multiplexer_8 (
    .in1(DR), .in2(AC), .in3({IR[15:12], I, IR[10:0]}), .in4({{5{1'b0}}, PC}), .in5({{5{1'b0}}, AR}),
    .in6(MEM), .out(B), .sel(priority_encoder_3_out), .en(or_29_out));  // open: in0, in7
  or or_29 (or_29_out, AC_B, IR_B, PC_B, AR_B, MEM_B);
  D_Flip_Flop d_ff_8 (.D(decoder_1_out7), .clk(clk), .Q(T7), .reset(or_20_out));  // open: Qn, preset

  // Other names for the same wires on the sheet: BBUS[10:0] = B[10:0]; IR[11] = I; T2 = IR_B
endmodule

module ALU (
  input  [7:0] INPR,
  input  [15:0] DR,
  input  [15:0] AC_in,
  input  [1:0] SLCT,
  output Z,
  output E,
  output [15:0] AC_out
);

  wire [15:0] adder_1_out, and_1_out, bit_extender_1_out, not_1_out;

  assign bit_extender_1_out = {{8{1'b0}}, INPR};  // Bit_Extender bit_extender_1
  assign and_1_out = AC_in & DR;  // AND_Gate and_1, 16 bits wide
  assign not_1_out = ~AC_in;  // NOT_Gate not_1, 16 bits wide
  Adder #(.width(16)) adder_1 (.a(AC_in), .b(DR), .out(adder_1_out), .cout(E));  // open: cin
  Multiplexer #(.select(2), .width(16)) multiplexer_1 (
    .in0(adder_1_out), .in1(and_1_out), .in2(bit_extender_1_out), .in3(not_1_out), .out(AC_out), .sel(SLCT));  // open: en
  nor nor_1 (Z, AC_out[0], AC_out[1], AC_out[2], AC_out[3], AC_out[4], AC_out[5], AC_out[6], AC_out[7], AC_out[8], AC_out[9], AC_out[10], AC_out[11], AC_out[12], AC_out[13], AC_out[14], AC_out[15]);
endmodule
